# Fritzing sketch pool cover (saved by Fritzing 0.9.3b)
breadboards: 1

parts:
  Ruggeduino_ET = Arduino Uno (Rev3)
  R1_Position_Sensor = Rotary Potentiometer (Small) [maximum_resistance=100kΩ package=THT]
  S1_on_south_Wall = Toggle Switch [package=THT]
  12_Volt_DC_Power_Supply = DC Power [voltage=5]
  D1 = Rectifier Diode [part_number=1N4001 package="300 mil [THT]"]
  D2 = Rectifier Diode [part_number=1N4001 package="300 mil [THT]"]
  S2_Calibrate_on/off_Switch = Toggle Switch [package=THT]
  S3_Set_upper_and_lower_limits = Toggle Switch [package=THT]
  RL1_-_Raise_Relay = RELAY-2 [package=relay-g5v]
  RL2_-_Lower_Relay = RELAY-2 [package=relay-g5v]
  R2 = Resistor [tolerance=±5% resistance=220 package=THT]
  R3 = Resistor [tolerance=±5% resistance=220 package=THT]
  R4 = Resistor [tolerance=±5% resistance=220 package=THT]
  R5 = Resistor [tolerance=±5% resistance=220 package=THT]  # not connected
  R6 = Resistor [tolerance=±5% resistance=220 package=THT]
  R7 = Resistor [tolerance=±5% resistance=220 package=THT]
  R8 = Resistor [tolerance=±5% resistance=220 package=THT]
  R9 = Resistor [tolerance=±5% resistance=220 package=THT]
  R10 = Resistor [tolerance=±5% resistance=220 package=THT]
  S4_Manual_Raise/Lower = Toggle Switch [package=THT]
  S5_Monitor_on/off = Toggle Switch [package=THT]
  R11 = Resistor [tolerance=±5% resistance=220 package=THT]
  Up_Relay_at_Motor = Resistor [tolerance=±5% resistance=220 package=THT]
  Down_Relay_at_Motor_no_wire_color = Resistor [tolerance=±5% resistance=220 package=THT]
  C1 = Ceramic Capacitor [capacitance=100nF package="100 mil [THT, multilayer]"]
  S4_Manual_Raise/Lower1 = Toggle Switch [package=THT]

nets:
  N1: Ruggeduino_ET.A0, R1_Position_Sensor.wiper, C1.1
  N2: Ruggeduino_ET.D9_PWM, S3_Set_upper_and_lower_limits.L1, R10.Pin_0
  N3: Ruggeduino_ET.D13/SCK, S5_Monitor_on/off.L2, R11.Pin_0
  N4: Ruggeduino_ET.GND, R1_Position_Sensor.leg1, 12_Volt_DC_Power_Supply.V-, R6.Pin_1, C1.0
  N5: Ruggeduino_ET.D2, R3.Pin_1, R6.Pin_0
  N6: Ruggeduino_ET.D3_PWM, R7.Pin_0
  N7: Ruggeduino_ET.D4, RL1_-_Raise_Relay.2
  N8: Ruggeduino_ET.D5_PWM, S2_Calibrate_on/off_Switch.L2, R8.Pin_0
  N9: Ruggeduino_ET.D6_PWM, S3_Set_upper_and_lower_limits.L2, R9.Pin_0
  N10: Ruggeduino_ET.D7, RL2_-_Lower_Relay.2
  N11: Ruggeduino_ET.5V, R1_Position_Sensor.leg2, S3_Set_upper_and_lower_limits.COM
  N12: S1_on_south_Wall.COM, 12_Volt_DC_Power_Supply.V+, RL2_-_Lower_Relay.5
  N13: S1_on_south_Wall.L2, D2.anode, R2.Pin_1
  N14: D1.cathode, D2.cathode
  N15: D1.anode, R4.Pin_1
  N16: RL1_-_Raise_Relay.10, S4_Manual_Raise/Lower.L1, Up_Relay_at_Motor.Pin_0, S4_Manual_Raise/Lower1.L2
  N17: RL2_-_Lower_Relay.10, S4_Manual_Raise/Lower.L2, Down_Relay_at_Motor_no_wire_color.Pin_0

notes:
  10K
  S1 switch on the south wall
  all resistors are 10K
  S2 calibrate on/off switch
  S3 set up or lown limit
  S4 maual up/down switch
  S5 turn monitor on/off
